// Logisim project JK Display try 1.circ as structural Verilog: 2 circuits, main circuit main
module main (
  input  in_1
);

  wire circuit_1_a_2, circuit_1_b_2, circuit_1_c_2, circuit_1_d, circuit_1_e, circuit_1_f, circuit_1_g,
       clock_1_out, j_k_ff_1_q, j_k_ff_1_qn, j_k_ff_2_q, j_k_ff_2_qn, j_k_ff_3_q;

  Clock clock_1 (.out(clock_1_out));
  J_K_Flip_Flop j_k_ff_1 (
    .J(in_1), .clk(clock_1_out), .K(in_1), .Q(j_k_ff_1_q), .Qn(j_k_ff_1_qn));  // open: preset, en, reset
  circuit circuit_1 (
    .A(j_k_ff_3_q), .B(j_k_ff_2_q), .C(j_k_ff_1_q), .a_2(circuit_1_a_2), .b_2(circuit_1_b_2),
    .c_2(circuit_1_c_2), .d(circuit_1_d), .e(circuit_1_e), .f(circuit_1_f), .g(circuit_1_g));
  J_K_Flip_Flop j_k_ff_2 (
    .J(in_1), .clk(j_k_ff_1_qn), .K(in_1), .Q(j_k_ff_2_q), .Qn(j_k_ff_2_qn));  // open: preset, en, reset
  _7_Segment_Display u_7_segment_display_1 (
    .g(circuit_1_g), .f(circuit_1_f), .a(circuit_1_a_2), .b(circuit_1_b_2), .e(circuit_1_e), .d(circuit_1_d),
    .c(circuit_1_c_2));  // open: dp
  J_K_Flip_Flop j_k_ff_3 (.J(in_1), .clk(j_k_ff_2_qn), .K(in_1), .Q(j_k_ff_3_q));  // open: Qn, preset, en, reset
endmodule

module circuit (
  input  A,
  input  B,
  input  C,
  output a_2,
  output b_2,
  output c_2,
  output d,
  output e,
  output f,
  output g
);

  wire and_1_out, and_2_out, and_3_out, and_4_out, and_5_out, and_6_out, and_7_out, and_8_out, and_9_out,
       and_10_out, and_11_out, and_12_out, and_13_out, and_14_out, and_15_out, and_16_out, and_17_out,
       and_18_out, and_19_out, and_20_out, and_21_out, not_1_out, not_2_out, not_3_out, not_4_out, not_5_out,
       not_6_out, not_7_out, not_8_out, not_9_out, not_10_out, not_11_out, not_12_out, not_13_out,
       not_14_out, not_15_out, not_16_out, not_17_out, not_18_out, not_19_out, not_20_out, not_21_out,
       not_22_out, not_23_out, not_24_out, not_25_out;

  not not_1 (not_1_out, A);
  not not_2 (not_2_out, B);
  not not_3 (not_3_out, A);
  not not_4 (not_4_out, C);
  not not_5 (not_5_out, C);
  not not_6 (not_6_out, A);
  not not_7 (not_7_out, B);
  not not_8 (not_8_out, B);
  not not_9 (not_9_out, C);
  not not_10 (not_10_out, A);
  not not_11 (not_11_out, B);
  not not_12 (not_12_out, A);
  not not_13 (not_13_out, C);
  not not_14 (not_14_out, A);
  not not_15 (not_15_out, C);
  not not_16 (not_16_out, A);
  not not_17 (not_17_out, B);
  not not_18 (not_18_out, A);
  not not_19 (not_19_out, C);
  not not_20 (not_20_out, B);
  not not_21 (not_21_out, C);
  not not_22 (not_22_out, A);
  not not_23 (not_23_out, A);
  not not_24 (not_24_out, B);
  not not_25 (not_25_out, C);
  and and_1 (and_1_out, not_1_out, not_2_out);
  and and_2 (and_2_out, not_3_out, not_4_out);
  and and_3 (and_3_out, A, B);
  and and_4 (and_4_out, A, not_5_out);
  and and_5 (and_5_out, A, B);
  and and_6 (and_6_out, not_6_out, not_7_out, C);
  and and_7 (and_7_out, A, not_8_out, not_9_out);
  and and_8 (and_8_out, A, B, C);
  and and_9 (and_9_out, not_10_out, not_11_out);
  and and_10 (and_10_out, not_12_out, not_13_out);
  and and_11 (and_11_out, A, B);
  and and_12 (and_12_out, not_14_out, not_15_out);
  and and_13 (and_13_out, A, B);
  and and_14 (and_14_out, not_16_out, not_17_out);
  and and_15 (and_15_out, not_18_out, not_19_out);
  and and_16 (and_16_out, not_20_out, not_21_out);
  and and_17 (and_17_out, A, B, C);
  and and_18 (and_18_out, not_22_out, C);
  and and_19 (and_19_out, not_23_out, B);
  and and_20 (and_20_out, A, not_24_out);
  and and_21 (and_21_out, A, not_25_out);
  or or_1 (a_2, and_1_out, and_2_out, and_3_out);
  or or_2 (b_2, and_4_out, and_5_out);
  or or_3 (c_2, and_6_out, and_7_out, and_8_out);
  or or_4 (d, and_9_out, and_10_out, and_11_out);
  or or_5 (e, and_12_out, and_13_out);
  or or_6 (f, and_14_out, and_15_out, and_16_out, and_17_out);
  or or_7 (g, and_18_out, and_19_out, and_20_out, and_21_out);
endmodule
