// Logisim project using NAND gate.circ as structural Verilog: 2 circuits, main circuit main
module main (
  input  A,
  input  B,
  input  C
);

  wire circuit_1_a_2, circuit_1_b_2, circuit_1_c_2, circuit_1_d, circuit_1_e, circuit_1_f, circuit_1_g;

  circuit circuit_1 (
    .A(A), .B(B), .C(C), .a_2(circuit_1_a_2), .b_2(circuit_1_b_2), .c_2(circuit_1_c_2), .d(circuit_1_d),
    .e(circuit_1_e), .f(circuit_1_f), .g(circuit_1_g));
  _7_Segment_Display u_7_segment_display_1 (
    .g(circuit_1_g), .f(circuit_1_f), .a(circuit_1_a_2), .b(circuit_1_b_2), .e(circuit_1_e), .d(circuit_1_d),
    .c(circuit_1_c_2));  // open: dp
endmodule

module circuit (
  input  A,
  input  B,
  input  C,
  output a_2,
  output b_2,
  output c_2,
  output d,
  output e,
  output f,
  output g
);

  wire nand_1_out, nand_2_out, nand_3_out, nand_4_out, nand_5_out, nand_6_out, nand_7_out, nand_8_out,
       nand_9_out, nand_10_out, nand_11_out, nand_12_out, nand_13_out, nand_14_out, nand_15_out, nand_16_out,
       nand_17_out, nand_18_out, nand_19_out, nand_20_out, nand_21_out, nand_22_out, nand_23_out,
       nand_24_out, nand_25_out, nand_26_out, nand_27_out, nand_28_out, nand_29_out, nand_30_out,
       nand_31_out, nand_32_out, nand_33_out, nand_34_out, nand_35_out, nand_36_out, nand_37_out,
       nand_38_out, nand_39_out, nand_40_out, nand_41_out, nand_42_out, nand_43_out, nand_44_out,
       nand_45_out, nand_46_out;

  nand nand_1 (nand_1_out, A, A);
  nand nand_2 (nand_2_out, B, B);
  nand nand_3 (nand_3_out, A, A);
  nand nand_4 (nand_4_out, C, C);
  nand nand_5 (nand_5_out, C, C);
  nand nand_6 (nand_6_out, A, A);
  nand nand_7 (nand_7_out, B, B);
  nand nand_8 (nand_8_out, B, B);
  nand nand_9 (nand_9_out, C, C);
  nand nand_10 (nand_10_out, A, A);
  nand nand_11 (nand_11_out, B, B);
  nand nand_12 (nand_12_out, A, A);
  nand nand_13 (nand_13_out, C, C);
  nand nand_14 (nand_14_out, A, A);
  nand nand_15 (nand_15_out, C, C);
  nand nand_16 (nand_16_out, A, A);
  nand nand_17 (nand_17_out, B, B);
  nand nand_18 (nand_18_out, A, A);
  nand nand_19 (nand_19_out, C, C);
  nand nand_20 (nand_20_out, B, B);
  nand nand_21 (nand_21_out, C, C);
  nand nand_22 (nand_22_out, A, A);
  nand nand_23 (nand_23_out, A, A);
  nand nand_24 (nand_24_out, B, B);
  nand nand_25 (nand_25_out, C, C);
  nand nand_26 (nand_26_out, nand_1_out, nand_2_out);
  nand nand_27 (nand_27_out, nand_3_out, nand_4_out);
  nand nand_28 (nand_28_out, A, B);
  nand nand_29 (nand_29_out, A, nand_5_out);
  nand nand_30 (nand_30_out, A, B);
  nand nand_31 (nand_31_out, nand_6_out, nand_7_out, C);
  nand nand_32 (nand_32_out, A, nand_8_out, nand_9_out);
  nand nand_33 (nand_33_out, A, B, C);
  nand nand_34 (nand_34_out, nand_10_out, nand_11_out);
  nand nand_35 (nand_35_out, nand_12_out, nand_13_out);
  nand nand_36 (nand_36_out, A, B);
  nand nand_37 (nand_37_out, nand_14_out, nand_15_out);
  nand nand_38 (nand_38_out, A, B);
  nand nand_39 (nand_39_out, nand_16_out, nand_17_out);
  nand nand_40 (nand_40_out, nand_18_out, nand_19_out);
  nand nand_41 (nand_41_out, nand_20_out, nand_21_out);
  nand nand_42 (nand_42_out, A, B, C);
  nand nand_43 (nand_43_out, nand_22_out, C);
  nand nand_44 (nand_44_out, nand_23_out, B);
  nand nand_45 (nand_45_out, A, nand_24_out);
  nand nand_46 (nand_46_out, A, nand_25_out);
  nand nand_47 (a_2, nand_26_out, nand_27_out, nand_28_out);
  nand nand_48 (b_2, nand_29_out, nand_30_out);
  nand nand_49 (c_2, nand_31_out, nand_32_out, nand_33_out);
  nand nand_50 (d, nand_34_out, nand_35_out, nand_36_out);
  nand nand_51 (e, nand_37_out, nand_38_out);
  nand nand_52 (f, nand_39_out, nand_40_out, nand_41_out, nand_42_out);
  nand nand_53 (g, nand_43_out, nand_44_out, nand_45_out, nand_46_out);
endmodule
